# Fritzing sketch zapatobb (saved by Fritzing 0.9.6b)

parts:
  Componente4 = LilyPad Arduino USB
  Mod1 = KY-013 Analog Temperature Sensor Module [package="Breakout board"]
  MAX30102_Sensor1 = MAX30102 Oximeter and Heart-Rate Sensor [part_number=MAX30102]

nets:
  VIN: Componente4.3V3, Mod1.Vin, MAX30102_Sensor1.VIN
  GND: Componente4.GND, Mod1.-, MAX30102_Sensor1.GND
  N1: Componente4.A2, Mod1.S
  N2: Componente4.D10, MAX30102_Sensor1.SCL
  N3: Componente4.D11, MAX30102_Sensor1.SDA

custom parts:
  KY-013 Analog Temperature Sensor Module: KY-013 Analog Temperature Sensor module, measures ambient temperature based on resistance of the thermistor.
  MAX30102 Oximeter and Heart-Rate Sensor: The MAX30102 is an integrated pulse oximetry and heart-rate monitor biosensor module. It includes internal LEDs, photodetectors, optical elements, and low-noise electronics with ambient light rejection. The MAX30102 operates on a single 1.8V power supply and a separate 3.3V power supply for the internal LEDs. Communication is through a I2C-compatible interface.
